// Digital circuit ALU.dig as structural Verilog
module ALU (
);

  wire comparator_1_eq, comparator_2_eq, comparator_3_eq, comparator_4_eq, comparator_5_eq, comparator_6_eq,
       comparator_7_eq, comparator_8_eq, comparator_9_eq, comparator_10_eq, comparator_11_eq,
       comparator_12_eq, comparator_13_eq, comparator_14_eq, comparator_16_eq, comparator_17_eq,
       comparator_18_eq, comparator_19_eq, comparator_20_eq, comparator_21_eq, comparator_22_eq,
       comparator_23_eq, flag_register_1_p1, flag_register_1_p2, flag_register_1_p3, flag_register_1_p4,
       flag_register_1_p5, flag_register_1_p10, flag_register_1_p12;
  wire [7:0] binary_xor_1_p1, flag_register_1_p11, shift_register_1_p3, undriven;
  wire [7:1] undriven_2, undriven_3, undriven_4, undriven_5, undriven_6, undriven_7, undriven_8, undriven_9,
       undriven_10, undriven_11, undriven_12, undriven_13, undriven_14, undriven_15, undriven_16,
       undriven_17, undriven_18, undriven_19, undriven_20, undriven_21, undriven_22, undriven_23;

  Comparator #(.Bits(8)) comparator_1 (.a(undriven), .b({undriven_2, 1'b1}), .eq(comparator_1_eq));  // open: gt, lt
  Comparator #(.Bits(8)) comparator_2 (.a(undriven), .b({undriven_3, 1'b1}), .eq(comparator_2_eq));  // open: gt, lt
  Comparator #(.Bits(8)) comparator_3 (.a(undriven), .b({undriven_4, 1'b1}), .eq(comparator_3_eq));  // open: gt, lt
  Comparator #(.Bits(8)) comparator_4 (.a(undriven), .b({undriven_5, 1'b1}), .eq(comparator_4_eq));  // open: gt, lt
  Comparator #(.Bits(8)) comparator_5 (.a(undriven), .b({undriven_6, 1'b1}), .eq(comparator_5_eq));  // open: gt, lt
  Comparator #(.Bits(8)) comparator_6 (.a(undriven), .b({undriven_7, 1'b1}), .eq(comparator_6_eq));  // open: gt, lt
  Comparator #(.Bits(8)) comparator_7 (.a(undriven), .b({undriven_8, 1'b1}), .eq(comparator_7_eq));  // open: gt, lt
  Comparator #(.Bits(8)) comparator_8 (.a(undriven), .b({undriven_9, 1'b1}), .eq(comparator_8_eq));  // open: gt, lt
  Comparator #(.Bits(8)) comparator_9 (.a(undriven), .b({undriven_10, 1'b1}), .eq(comparator_9_eq));  // open: gt, lt
  Comparator #(.Bits(8)) comparator_10 (.a(undriven), .b({undriven_11, 1'b1}), .eq(comparator_10_eq));  // open: gt, lt
  Comparator #(.Bits(8)) comparator_11 (.a(undriven), .b({undriven_12, 1'b1}), .eq(comparator_11_eq));  // open: gt, lt
  Comparator #(.Bits(8)) comparator_12 (.a(undriven), .b({undriven_13, 1'b1}), .eq(comparator_12_eq));  // open: gt, lt
  Comparator #(.Bits(8)) comparator_13 (.a(undriven), .b({undriven_14, 1'b1}), .eq(comparator_13_eq));  // open: gt, lt
  Comparator #(.Bits(8)) comparator_14 (.a(undriven), .b({undriven_15, 1'b1}), .eq(comparator_14_eq));  // open: gt, lt
  // Flag_Register flag_register_1: pin names not known; wires that end beside it: flag_register_1_p1, flag_register_1_p2, flag_register_1_p3, flag_register_1_p4, flag_register_1_p5, comparator_1_eq, comparator_2_eq, comparator_3_eq, comparator_4_eq, flag_register_1_p10, flag_register_1_p11, flag_register_1_p12
  Adder_Subtractor adder_subtractor_1 (
    .C_in(flag_register_1_p12), .A(shift_register_1_p3), .B(binary_xor_1_p1), .ADD(comparator_5_eq),
    .ADC(comparator_6_eq), .SUB(comparator_7_eq), .CLK(flag_register_1_p10), .Q(flag_register_1_p11),
    .C_8(flag_register_1_p2), .F(flag_register_1_p3), .STC(flag_register_1_p4), .STF(flag_register_1_p5));
  Incrementor incrementor_1 (
    .C(binary_xor_1_p1), .INC(comparator_8_eq), .DEC(comparator_9_eq), .CLK(flag_register_1_p10),
    .Q(flag_register_1_p11));  // open: C_8, F, STC, STF, Q_S
  Comparator comparator_15 (
    .A(shift_register_1_p3), .B(binary_xor_1_p1), .CMP_bigger(comparator_10_eq),
    .CMP_equal(comparator_11_eq), .CMP_smaller(comparator_12_eq), .CLK(flag_register_1_p10),
    .Q(flag_register_1_p11));
  // Shift_Register shift_register_1: pin names not known; wires that end beside it: flag_register_1_p1, flag_register_1_p10, shift_register_1_p3, flag_register_1_p1, comparator_13_eq, comparator_14_eq, flag_register_1_p10, flag_register_1_p11, flag_register_1_p11
  Comparator #(.Bits(8)) comparator_16 (.a(undriven), .b({undriven_16, 1'b1}), .eq(comparator_16_eq));  // open: gt, lt
  Comparator #(.Bits(8)) comparator_17 (.a(undriven), .b({undriven_17, 1'b1}), .eq(comparator_17_eq));  // open: gt, lt
  Comparator #(.Bits(8)) comparator_18 (.a(undriven), .b({undriven_18, 1'b1}), .eq(comparator_18_eq));  // open: gt, lt
  Comparator #(.Bits(8)) comparator_19 (.a(undriven), .b({undriven_19, 1'b1}), .eq(comparator_19_eq));  // open: gt, lt
  Comparator #(.Bits(8)) comparator_20 (.a(undriven), .b({undriven_20, 1'b1}), .eq(comparator_20_eq));  // open: gt, lt
  Comparator #(.Bits(8)) comparator_21 (.a(undriven), .b({undriven_21, 1'b1}), .eq(comparator_21_eq));  // open: gt, lt
  Comparator #(.Bits(8)) comparator_22 (.a(undriven), .b({undriven_22, 1'b1}), .eq(comparator_22_eq));  // open: gt, lt
  Comparator #(.Bits(8)) comparator_23 (.a(undriven), .b({undriven_23, 1'b1}), .eq(comparator_23_eq));  // open: gt, lt
  Bitwise_NOT bitwise_not_1 (
    .A(shift_register_1_p3), .EN(comparator_16_eq), .CLK(flag_register_1_p10), .Q(flag_register_1_p11));
  Bitwise_OR bitwise_or_1 (
    .A(shift_register_1_p3), .B(binary_xor_1_p1), .EN(comparator_17_eq), .CLK(flag_register_1_p10));  // open: Q
  Bitwise_AND bitwise_and_1 (
    .A(shift_register_1_p3), .B(binary_xor_1_p1), .EN(comparator_18_eq), .CLK(flag_register_1_p10),
    .Q(flag_register_1_p11));
  Bitwise_XOR bitwise_xor_1 (
    .A(shift_register_1_p3), .B(binary_xor_1_p1), .EN(comparator_19_eq), .CLK(flag_register_1_p10),
    .Q(flag_register_1_p11));
  Binary_NOT binary_not_1 (
    .A(shift_register_1_p3[0]), .EN(comparator_20_eq), .CLK(flag_register_1_p10), .Q(flag_register_1_p11));
  Binary_OR binary_or_1 (
    .A(shift_register_1_p3[0]), .B(binary_xor_1_p1[0]), .EN(comparator_21_eq), .CLK(flag_register_1_p10),
    .Q(flag_register_1_p11));
  Binary_AND binary_and_1 (
    .A(shift_register_1_p3[0]), .B(binary_xor_1_p1[0]), .EN(comparator_22_eq), .CLK(flag_register_1_p10),
    .Q(flag_register_1_p11));
  // Binary_XOR binary_xor_1: pin names not known; wires that end beside it: binary_xor_1_p1, flag_register_1_p1, flag_register_1_p10, shift_register_1_p3, binary_xor_1_p1, comparator_23_eq, flag_register_1_p10, flag_register_1_p11, flag_register_1_p11
  // Pins of 1 and 8 bits meet at shift_register_1_p3
  // Pins of 1 and 8 bits meet at binary_xor_1_p1
  // Pins of 1 and 8 bits meet at {undriven_6, 1'b1}
  // Pins of 1 and 8 bits meet at {undriven_7, 1'b1}
  // Pins of 1 and 8 bits meet at {undriven_8, 1'b1}
  // Pins of 1 and 8 bits meet at {undriven_11, 1'b1}
  // Pins of 1 and 8 bits meet at {undriven_12, 1'b1}
  // Pins of 1 and 8 bits meet at {undriven_13, 1'b1}
  // Pins of 1 and 8 bits meet at {undriven_16, 1'b1}
  // Pins of 1 and 8 bits meet at {undriven_17, 1'b1}
  // Pins of 1 and 8 bits meet at {undriven_18, 1'b1}
  // Pins of 1 and 8 bits meet at {undriven_19, 1'b1}

  // Notes on the sheet:
  //   CMD
  //   A
  //   B
  //   C
  //   DAT
  //   CLK
  //   Q
endmodule
