// Digital circuit CPU.dig as structural Verilog
module CPU (
  input  clk,
  input  CLR_PC,
  input  STR
);

  wire comparator_1_eq, comparator_2_eq, comparator_3_eq, comparator_4_eq, comparator_5_eq, comparator_6_eq,
       comparator_7_eq, comparator_8_eq, comparator_9_eq, comparator_10_eq, comparator_11_eq,
       flash_memory_1_p2, flash_memory_1_p3;
  wire [3:0] register_2_val, register_2_val_2;
  wire [7:0] dipswitch_1_out, flash_memory_1_p5, flash_memory_1_p6;
  wire [15:0] flash_memory_1_p7, programme_counter_1_ln;

  LED led_1 (.in(dipswitch_1_out[0]));
  LED led_2 (.in(dipswitch_1_out[1]));
  DipSwitch dipswitch_1 (.out(dipswitch_1_out[0]));
  DipSwitch dipswitch_2 (.out(dipswitch_1_out[1]));
  LED led_3 (.in(dipswitch_1_out[2]));
  LED led_4 (.in(dipswitch_1_out[3]));
  DipSwitch dipswitch_3 (.out(dipswitch_1_out[2]));
  DipSwitch dipswitch_4 (.out(dipswitch_1_out[3]));
  LED led_5 (.in(dipswitch_1_out[4]));
  LED led_6 (.in(dipswitch_1_out[5]));
  DipSwitch dipswitch_5 (.out(dipswitch_1_out[4]));
  DipSwitch dipswitch_6 (.out(dipswitch_1_out[5]));
  LED led_7 (.in(dipswitch_1_out[6]));
  LED led_8 (.in(dipswitch_1_out[7]));
  DipSwitch dipswitch_7 (.out(dipswitch_1_out[6]));
  DipSwitch dipswitch_8 (.out(dipswitch_1_out[7]));
  Comparator #(.Bits(8)) comparator_1 (.a(flash_memory_1_p5), .b(8'h1), .eq(comparator_1_eq));  // open: gt, lt
  Comparator #(.Bits(8)) comparator_2 (.a(flash_memory_1_p5), .b(8'h2), .eq(comparator_2_eq));  // open: gt, lt
  Comparator #(.Bits(8)) comparator_3 (.a(flash_memory_1_p5), .b(8'h3), .eq(comparator_3_eq));  // open: gt, lt
  Comparator #(.Bits(8)) comparator_4 (.a(flash_memory_1_p5), .b(8'h4), .eq(comparator_4_eq));  // open: gt, lt
  Comparator #(.Bits(8)) comparator_5 (.a(flash_memory_1_p5), .b(8'h5), .eq(comparator_5_eq));  // open: gt, lt
  Comparator #(.Bits(8)) comparator_6 (.a(flash_memory_1_p5), .b(8'h6), .eq(comparator_6_eq));  // open: gt, lt
  Comparator #(.Bits(8)) comparator_7 (.a(flash_memory_1_p5), .b(8'h7), .eq(comparator_7_eq));  // open: gt, lt
  Comparator #(.Bits(8)) comparator_8 (.a(flash_memory_1_p5), .b(8'h26), .eq(comparator_8_eq));  // open: gt, lt
  Comparator #(.Bits(8)) comparator_9 (.a(flash_memory_1_p5), .b(8'h27), .eq(comparator_9_eq));  // open: gt, lt
  Comparator #(.Bits(8)) comparator_10 (.a(flash_memory_1_p5), .b(8'h28), .eq(comparator_10_eq));  // open: gt, lt
  Comparator #(.Bits(8)) comparator_11 (.a(flash_memory_1_p5), .b(8'h29), .eq(comparator_11_eq));  // open: gt, lt
  Programme_Counter programme_counter_1 (
    .DAT(flash_memory_1_p6), .ADR(flash_memory_1_p7), .CLK(clk), .JMP(comparator_1_eq),
    .CJP(comparator_2_eq), .CLR(CLR_PC), .LN(programme_counter_1_ln));
  // Flash_Memory flash_memory_1: pin names not known; wires that end beside it: programme_counter_1_ln, flash_memory_1_p2, flash_memory_1_p3, clk, flash_memory_1_p5, flash_memory_1_p6, flash_memory_1_p7
  // ALU alu_1: pin names not known; wires that end beside it: flash_memory_1_p5, flash_memory_1_p6, clk, flash_memory_1_p6, flash_memory_1_p2
  // DAT_to_ADR_interface dat_to_adr_interface_1: pin names not known; wires that end beside it: flash_memory_1_p6, comparator_3_eq, comparator_4_eq, comparator_5_eq, clk, flash_memory_1_p7, flash_memory_1_p3
  // RAM ram_1: pin names not known; wires that end beside it: flash_memory_1_p6, flash_memory_1_p7, comparator_6_eq, comparator_7_eq, clk, flash_memory_1_p6
  Register register_1 (
    .D(dipswitch_1_out), .STR(STR), .LD(comparator_8_eq), .CLK(clk), .Q(flash_memory_1_p6));  // open: VAL
  Input_Control input_control_1 (.INP(STR), .LD(comparator_9_eq), .CLK(clk), .Q(flash_memory_1_p6));
  Register register_2 (
    .D(flash_memory_1_p6), .STR(comparator_10_eq), .LD(comparator_11_eq), .CLK(clk),
    .VAL({register_2_val_2, register_2_val}), .Q(flash_memory_1_p6));
  Seven_Seg_Hex seven_seg_hex_1 (.d(register_2_val), .dp(1'b0));
  Seven_Seg_Hex seven_seg_hex_2 (.d(register_2_val_2), .dp(1'b0));
  LED led_9 (.in(register_2_val[0]));
  LED led_10 (.in(register_2_val[1]));
  LED led_11 (.in(register_2_val[2]));
  LED led_12 (.in(register_2_val[3]));
  LED led_13 (.in(register_2_val_2[0]));
  LED led_14 (.in(register_2_val_2[1]));
  LED led_15 (.in(register_2_val_2[2]));
  LED led_16 (.in(register_2_val_2[3]));

  // Notes on the sheet:
  //   clk: Hz: 5
  //   CMD
  //   DAT
  //   ADR
  //   CLK
  //   LN: current line of code being executed
  //   commands requiring the address bus to be disabled:
  //   Bus Transfer:
  //   - load from interface registers
  //   commands requiring the data bus to be disabled:
  //   Storage: 
  //   - load > data
  //   ALU:
  //   - add > data
  //   - add with carry > data
  //   - subtract > data
  //   incrementor:
  //   - increment > data
  //   - decrement > data
  //   logic:
  //   - binary not
  //   - binary or
  //   - binary and
  //   - binary xor
  //   - bitwise not
  //   - bitwise or
  //   - bitwise and
  //   - bitwise xor
  //   a/b/c registers:
  //   - load a > data
  //   - load b > data
  //   - load c > data
  //   compare:
  //   - bigger > data
  //   - equal > data
  //   - smaller > data
  //   flag reg:
  //   - load carry > data
  //   - load overflow > data
  //   - load flags > data
endmodule
