// Digital circuit Flash Memory.dig as structural Verilog
module Flash_Memory (
  input  [15:0] LN,
  input  DAT_dis,
  input  ADR_dis,
  input  CLK,
  output [7:0] Q_CMD,
  output [7:0] Q_DAT,
  output [15:0] Q_ADR
);

  wire d_ff_1_nq, d_ff_2_nq, delay_1_out;

  Delay delay_1 (.in(CLK), .out(delay_1_out));
  D_FF d_ff_1 (.D(DAT_dis), .C(delay_1_out), .nQ(d_ff_1_nq));  // open: Q
  D_FF d_ff_2 (.D(ADR_dis), .C(delay_1_out), .nQ(d_ff_2_nq));  // open: Q
  ROM #(.AddrBits(16), .isProgramMemory("true"), .Bits(8)) CMD (.A(LN), .sel(1'b1), .D(Q_CMD));
  ROM #(.AddrBits(16), .isProgramMemory("true"), .Bits(8)) DAT (.A(LN), .sel(d_ff_1_nq), .D(Q_DAT));
  ROM #(.AddrBits(16), .isProgramMemory("true"), .Bits(16)) ADR (.A(LN), .sel(d_ff_2_nq), .D(Q_ADR));

  // Notes on the sheet:
  //   DAT_dis / ADR_dis :
  //   disable the data / address bus
  //   for the next tick in order to
  //   avoid bus collisions
  //   - Flash memory
endmodule
